// Logisim project Y86Control.circ as structural Verilog: 19 circuits, main circuit Y86Control
module Y86Control (
  input  [3:0] icode,
  input  [3:0] ifun,
  input  [2:0] CC,
  input  [1:0] Stat,
  input  imemError,
  input  dmemError,
  output \continue ,
  output statWrite,
  output [1:0] statVal,
  output [1:0] PCIncSrc,
  output valCsrc,
  output valAsrc,
  output valBsrc,
  output [1:0] dstEsrc,
  output dstMsrc,
  output [1:0] aluAsrc,
  output aluBsrc,
  output setCC,
  output aluOp,
  output dmemAddr,
  output dmemData,
  output dmemWrite,
  output [1:0] newPC
);

  wire not_1_out, not_2_out;

  and and_1 (\continue , not_1_out, not_2_out);
  not not_1 (not_1_out, Stat[0]);
  not not_2 (not_2_out, Stat[1]);
  statV statv_1 (.icode(icode), .imemError(imemError), .dmemError(dmemError), .out_4(statVal));
  statW statw_1 (.icode(icode), .imemError(imemError), .dmemError(dmemError), .out_4(statWrite));
  PCIncrSrc pcincrsrc_1 (.out_5(PCIncSrc), .A(icode[3]), .B(icode[2]), .C(icode[1]), .D(icode[0]));
  ValCsrc valcsrc_1 (.out_5(valCsrc), .A(icode[3]), .B(icode[2]), .C(icode[1]), .D(icode[0]));
  valAsrc valasrc_1 (.out_5(valAsrc), .A(icode[3]), .B(icode[2]), .C(icode[1]), .D(icode[0]));
  dstEsrc dstesrc_1 (.CC(CC), .ifun(ifun), .icode(icode), .out_4(dstEsrc));
  valBsrc valbsrc_1 (.out_5(valBsrc), .A(icode[3]), .B(icode[2]), .C(icode[1]), .D(icode[0]));
  dstMsrc dstmsrc_1 (.out_5(dstMsrc), .A(icode[3]), .B(icode[2]), .C(icode[1]), .D(icode[0]));
  aluAsrc aluasrc_1 (.out_5(aluAsrc), .A(icode[3]), .B(icode[2]), .C(icode[1]), .D(icode[0]));
  aluBsrc alubsrc_1 (.out_5(aluBsrc), .A(icode[3]), .B(icode[2]), .C(icode[1]), .D(icode[0]));
  setCC setcc_1 (.out_5(setCC), .A(icode[3]), .B(icode[2]), .C(icode[1]), .D(icode[0]));
  aluOP aluop_1 (.out_5(aluOp), .A(icode[3]), .B(icode[2]), .C(icode[1]), .D(icode[0]));
  dmemAddr dmemaddr_1 (.out_5(dmemAddr), .A(icode[3]), .B(icode[2]), .C(icode[1]), .D(icode[0]));
  dmemData dmemdata_1 (.out_5(dmemData), .A(icode[3]), .B(icode[2]), .C(icode[1]), .D(icode[0]));
  dmemWrite dmemwrite_1 (.out_5(dmemWrite), .A(icode[3]), .B(icode[2]), .C(icode[1]), .D(icode[0]));
  newPC newpc_1 (.CC(CC), .ifun(ifun), .icode(icode), .out_4(newPC));
endmodule

// PCIcrSrc
module PCIncrSrc (
  input  A,
  input  B,
  input  C,
  input  D,
  output [1:0] out_5
);

  wire and_1_out, and_2_out, and_3_out, and_4_out, and_5_out, and_6_out, not_1_out, not_2_out, not_3_out,
       not_4_out;

  and and_1 (and_1_out, not_1_out, C, D);
  or or_1 (out_5[1], and_1_out, and_2_out, and_3_out);
  and and_2 (and_2_out, A, not_3_out);
  and and_3 (and_3_out, B, not_3_out);
  not not_1 (not_1_out, A);
  not not_2 (not_2_out, B);
  not not_3 (not_3_out, C);
  not not_4 (not_4_out, D);
  or or_2 (out_5[0], and_4_out, and_5_out, and_6_out);
  and and_4 (and_4_out, C, not_4_out);
  and and_5 (and_5_out, C, not_2_out);
  and and_6 (and_6_out, not_3_out, B);
endmodule

module ValCsrc (
  input  A,
  input  B,
  input  C,
  input  D,
  output out_5
);

  wire and_1_out, and_2_out, not_1_out, not_2_out, not_3_out;

  not not_1 (not_1_out, A);
  and and_1 (and_1_out, not_1_out, not_2_out);
  not not_2 (not_2_out, B);
  or or_1 (out_5, and_1_out, and_2_out);
  and and_2 (and_2_out, not_1_out, not_3_out);
  not not_3 (not_3_out, C);
endmodule

module dstEsrc (
  input  [2:0] CC,
  input  [3:0] icode,
  input  [3:0] ifun,
  output [1:0] out_4
);

  wire [0:0] condition_1_output;

  condition condition_1 (.CC(CC), .Const(1'b0), .ifun(ifun), .\output (condition_1_output[0]));
  Multiplexer #(.select(4), .width(2)) multiplexer_1 (
    .in0(2'b11), .in1(2'b11), .in2({1'b0, condition_1_output[0]}), .in3(2'b00), .in4(2'b11), .in5(2'b11),
    .in6(2'b00), .in7(2'b11), .in8(2'b01), .in9(2'b01), .in10(2'b01), .in11(2'b01), .out(out_4), .sel(icode));  // open: in12, in13, in14, in15, en
endmodule

module newPC (
  input  [2:0] CC,
  input  [3:0] icode,
  input  [3:0] ifun,
  output [1:0] out_4
);

  wire [1:1] condition_1_output;

  condition condition_1 (.CC(CC), .Const(1'b1), .ifun(ifun), .\output (condition_1_output[1]));
  Multiplexer #(.select(4), .width(2)) multiplexer_1 (
    .in0(2'b00), .in1(2'b00), .in2(2'b00), .in3(2'b00), .in4(2'b00), .in5(2'b00), .in6(2'b00),
    .in7({condition_1_output[1], 1'b0}), .in8(2'b01), .in9(2'b10), .in10(2'b00), .in11(2'b00), .out(out_4),
    .sel(icode));  // open: in12, in13, in14, in15, en
endmodule

module valAsrc (
  input  A,
  input  B,
  input  C,
  input  D,
  output out_5
);

  wire not_1_out;

  and and_1 (out_5, A, not_1_out, D);
  not not_1 (not_1_out, B);
endmodule

module valBsrc (
  input  A,
  input  B,
  input  C,
  input  D,
  output out_5
);


  assign out_5 = A;
endmodule

module dstMsrc (
  input  A,
  input  B,
  input  C,
  input  D,
  output out_5
);

  wire and_1_out, and_2_out, and_3_out, not_1_out, not_2_out, not_3_out, not_4_out;

  and and_1 (and_1_out, not_1_out, C, D);
  not not_1 (not_1_out, A);
  or or_1 (out_5, and_1_out, and_2_out, and_3_out, not_4_out);
  and and_2 (and_2_out, not_1_out, not_2_out);
  not not_2 (not_2_out, B);
  and and_3 (and_3_out, not_2_out, D, not_3_out);
  not not_3 (not_3_out, C);
  not not_4 (not_4_out, D);
endmodule

module aluAsrc (
  input  A,
  input  B,
  input  C,
  input  D,
  output [1:0] out_5
);

  wire and_1_out, and_2_out, and_3_out, not_1_out, not_2_out, not_3_out, not_4_out;

  not not_1 (not_1_out, A);
  and and_1 (and_1_out, A, not_2_out, not_4_out);
  not not_2 (not_2_out, B);
  not not_3 (not_3_out, C);
  or or_1 (out_5[0], and_1_out, and_2_out, and_3_out);
  and and_2 (and_2_out, not_3_out, not_1_out);
  and and_3 (and_3_out, not_1_out, C, D);
  not not_4 (not_4_out, D);

  assign out_5[1] = A;
endmodule

module aluBsrc (
  input  A,
  input  B,
  input  C,
  input  D,
  output out_5
);

  wire and_1_out, and_2_out, not_1_out, not_2_out, not_3_out, not_4_out;

  and and_1 (and_1_out, not_1_out, not_2_out);
  not not_1 (not_1_out, A);
  or or_1 (out_5, and_1_out, and_2_out);
  not not_2 (not_2_out, B);
  and and_2 (and_2_out, not_3_out, B, not_4_out);
  not not_3 (not_3_out, C);
  not not_4 (not_4_out, D);
endmodule

module setCC (
  input  A,
  input  B,
  input  C,
  input  D,
  output out_5
);

  wire not_1_out;

  and and_1 (out_5, B, not_1_out, C);
  not not_1 (not_1_out, D);
endmodule

module aluOP (
  input  A,
  input  B,
  input  C,
  input  D,
  output out_5
);

  and and_1 (out_5, B, C);
endmodule

module dmemAddr (
  input  A,
  input  B,
  input  C,
  input  D,
  output out_5
);

  wire not_1_out;

  and and_1 (out_5, A, not_1_out, D);
  not not_1 (not_1_out, B);
endmodule

module dmemData (
  input  A,
  input  B,
  input  C,
  input  D,
  output out_5
);

  wire not_1_out, not_2_out, not_3_out;

  and and_1 (out_5, A, not_1_out, not_2_out, not_3_out);
  not not_1 (not_1_out, B);
  not not_2 (not_2_out, C);
  not not_3 (not_3_out, D);
endmodule

module dmemWrite (
  input  A,
  input  B,
  input  C,
  input  D,
  output out_5
);

  wire and_1_out, and_2_out, not_1_out, not_2_out, not_3_out;

  or or_1 (out_5, and_1_out, and_2_out);
  and and_1 (and_1_out, A, not_1_out, not_3_out);
  not not_1 (not_1_out, B);
  and and_2 (and_2_out, A, not_1_out, not_2_out, not_3_out);
  not not_2 (not_2_out, C);
  not not_3 (not_3_out, D);
endmodule

// cond
module condition (
  input  Const,
  input  [2:0] CC,
  input  [3:0] ifun,
  output \output 
);

  wire and_1_out, not_1_out, not_2_out, or_1_out, xor_1_out;

  xor xor_1 (xor_1_out, CC[0], CC[1]);
  not not_1 (not_1_out, CC[2]);
  not not_2 (not_2_out, xor_1_out);
  or or_1 (or_1_out, xor_1_out, CC[2]);
  and and_1 (and_1_out, not_2_out, not_1_out);
  Multiplexer #(.select(4)) multiplexer_1 (
    .in0(Const), .in1(or_1_out), .in2(xor_1_out), .in3(CC[2]), .in4(not_1_out), .in5(not_2_out),
    .in6(and_1_out), .out(\output ), .sel(ifun));  // open: in7, in8, in9, in10, in11, in12, in13, in14, in15, en

  // Notes on the sheet:
  //   ZF
  //   OF
endmodule

module statW (
  input  [3:0] icode,
  input  imemError,
  input  dmemError,
  output out_4
);

  wire invalidinstr_1_out_5, multiplexer_1_out;

  invalidInstr invalidinstr_1 (.A(icode[0]), .B(icode[1]), .C(icode[2]), .D(icode[3]), .out_5(invalidinstr_1_out_5));
  Multiplexer #(.select(4)) multiplexer_1 (
    .in0(1'b0), .in1(1'b0), .in2(1'b0), .in3(1'b0), .in4(dmemError), .in5(dmemError), .in6(1'b0), .in7(1'b0),
    .in8(dmemError), .in9(dmemError), .in10(dmemError), .in11(dmemError), .out(multiplexer_1_out), .sel(icode));  // open: in12, in13, in14, in15, en
  or or_1 (out_4, invalidinstr_1_out_5, imemError, multiplexer_1_out);
endmodule

module statV (
  input  [3:0] icode,
  input  dmemError,
  input  imemError,
  output [1:0] out_4
);

  wire invalidinstr_1_out_5, multiplexer_1_out;

  invalidInstr invalidinstr_1 (.A(icode[0]), .B(icode[1]), .C(icode[2]), .D(icode[3]), .out_5(invalidinstr_1_out_5));
  Multiplexer multiplexer_1 (.in0(1'b0), .in1(dmemError), .out(multiplexer_1_out), .sel(out_4[1]));  // open: en
  or or_1 (out_4[1], imemError, dmemError);
  Multiplexer multiplexer_2 (
    .in0(invalidinstr_1_out_5), .in1(multiplexer_1_out), .out(out_4[0]), .sel(out_4[1]));  // open: en
endmodule

module invalidInstr (
  input  A,
  input  B,
  input  C,
  input  D,
  output out_5
);

  wire and_1_out, and_2_out, not_1_out, not_2_out, not_3_out, not_4_out;

  not not_1 (not_1_out, A);
  not not_2 (not_2_out, B);
  not not_3 (not_3_out, C);
  not not_4 (not_4_out, D);
  and and_1 (and_1_out, B, A);
  or or_1 (out_5, and_1_out, and_2_out);
  and and_2 (and_2_out, not_1_out, not_2_out, not_3_out, not_4_out);
endmodule
